// Logisim project ping_pong.circ as structural Verilog: 3 circuits, main circuit main
module main (
  input  in_1,
  input  in_2,
  output [6:0] out_3,
  output [4:0] out_4,
  output [4:0] out_5,
  output [4:0] out_6,
  output [4:0] out_7,
  output [4:0] out_8,
  output [4:0] out_9,
  output [4:0] out_10,
  output [4:0] out_11,
  output [4:0] out_12,
  output [4:0] out_13,
  output [4:0] out_14
);

  wire and_1_out, and_2_out, and_3_out, and_4_out, and_5_out, and_6_out, and_7_out, and_8_out, button_1_out,
       button_2_out, button_3_out, clock_1_out, clock_2_out, clock_3_out, clock_4_out, comparator_1_gt,
       comparator_2_lt, comparator_3_gt, comparator_4_gt, comparator_5_lt, comparator_6_eq, comparator_7_eq,
       comparator_8_eq, comparator_9_eq, comparator_10_lt, comparator_11_lt, comparator_12_lt,
       comparator_13_lt, comparator_14_gt, decoder_1_out0, decoder_1_out1, decoder_1_out2, decoder_1_out3,
       decoder_1_out4, decoder_1_out5, decoder_1_out6, decoder_1_out7, j_k_ff_1_q, j_k_ff_2_q,
       multiplexer_5_out, nor_1_out, nor_2_out, not_1_out, not_2_out, not_3_out, not_4_out, not_5_out,
       not_6_out, or_1_out, or_2_out, or_3_out, or_4_out, or_5_out, or_6_out, rgb_video_1_p1;
  wire [2:0] counter_7_q, register_3_q, subtractor_4_out;
  wire [2:2] multiplexer_4_out;
  wire [3:0] counter_6_q;
  wire [4:0] controlled_buffer_1_out, controlled_buffer_2_out, counter_4_q, counter_5_q, multiplexer_2_out,
       multiplexer_3_out, subtractor_2_out, subtractor_3_out;

  Clock #(.highDuration(32), .lowDuration(32)) clock_1 (.out(clock_1_out));
  or or_1 (or_1_out, in_1, comparator_5_lt);
  Clock clock_2 (.out(clock_2_out));
  Clock #(.highDuration(2), .lowDuration(2)) clock_3 (.out(clock_3_out));
  not not_1 (not_1_out, clock_3_out);
  Comparator #(.mode("unsigned"), .width(5)) comparator_1 (
    .a(counter_4_q), .b(5'b00011), .gt(comparator_1_gt));  // open: eq, lt
  and and_1 (and_1_out, comparator_1_gt, button_1_out, and_2_out);
  and and_2 (and_2_out, comparator_4_gt, clock_1_out);
  and and_3 (and_3_out, and_2_out, button_2_out, comparator_2_lt);
  Comparator #(.mode("unsigned"), .width(5)) comparator_2 (
    .a(counter_4_q), .b(5'b11100), .lt(comparator_2_lt));  // open: gt, eq
  Clock clock_4 (.out(clock_4_out));
  Counter #(.max('h7f), .width(7)) counter_1 (
    .clr(or_1_out), .count(1'b1), .clk(clock_2_out), .Q(out_3));  // open: load, up, D, carry
  and and_4 (and_4_out, comparator_3_gt, not_1_out);
  and and_5 (and_5_out, and_4_out, multiplexer_5_out);
  or or_2 (or_2_out, and_1_out, and_3_out);
  and and_6 (and_6_out, comparator_4_gt, clock_4_out);
  Counter #(.max('h1f), .width(5)) counter_2 (
    .clr(in_2), .load(and_8_out), .up(j_k_ff_1_q), .count(1'b1), .clk(and_4_out), .D(5'b01111), .Q(out_5));  // open: carry
  or or_3 (or_3_out, and_5_out, and_8_out);
  Counter #(.max('h1f), .width(5)) counter_3 (
    .load(and_8_out), .up(j_k_ff_2_q), .count(1'b1), .clk(or_3_out), .D(5'b01111), .Q(out_8));  // open: clr, carry
  Counter #(.max('h1f), .width(5)) counter_4 (
    .up(and_3_out), .count(1'b1), .clk(or_2_out), .D(5'b01111), .Q(counter_4_q));  // open: clr, load, carry
  Counter #(.max('h1f), .width(5)) counter_5 (
    .count(1'b1), .clk(and_6_out), .D(out_11), .Q(counter_5_q));  // open: clr, load, up, carry
  Comparator #(.mode("unsigned"), .width(7)) comparator_3 (
    .a(7'b0000010), .b(out_3), .gt(comparator_3_gt));  // open: eq, lt
  Comparator #(.mode("unsigned"), .width(7)) comparator_4 (
    .a(out_3), .b(7'b0000001), .gt(comparator_4_gt));  // open: eq, lt
  Comparator #(.mode("unsigned"), .width(7)) comparator_5 (
    .a(7'b0100011), .b(out_3), .lt(comparator_5_lt));  // open: gt, eq
  Register #(.width(5)) register_1 (.D(out_5), .en(1'b1), .clk(and_4_out), .Q(out_4));  // open: clr
  Register #(.width(5)) register_2 (.D(out_8), .en(1'b1), .clk(and_4_out), .Q(out_7));  // open: clr
  not not_2 (not_2_out, comparator_3_gt);
  assign controlled_buffer_1_out = and_4_out ? out_5 : 5'bz;  // Controlled_Buffer controlled_buffer_1
  Comparator #(.width(5)) comparator_6 (.a(5'b11110), .b(out_5), .eq(comparator_6_eq));  // open: gt, lt
  Comparator #(.width(5)) comparator_7 (.a(out_5), .b(5'b00001), .eq(comparator_7_eq));  // open: gt, lt
  assign controlled_buffer_2_out = and_4_out ? out_8 : 5'bz;  // Controlled_Buffer controlled_buffer_2
  Comparator #(.width(5)) comparator_8 (.a({5{1'b1}}), .b(out_8), .eq(comparator_8_eq));  // open: gt, lt
  Comparator #(.width(5)) comparator_9 (.a(out_8), .b({5{1'b0}}), .eq(comparator_9_eq));  // open: gt, lt
  Adder #(.width(5)) adder_1 (.a(counter_4_q), .b(5'b00011), .out(out_10));  // open: cin, cout
  Subtractor #(.width(5)) subtractor_1 (.a(counter_4_q), .b(5'b00011), .out(out_11));  // open: bin, bout
  Comparator #(.mode("unsigned"), .width(5)) comparator_10 (
    .a(out_10), .b(counter_5_q), .lt(comparator_10_lt));  // open: gt, eq
  Comparator #(.mode("unsigned"), .width(5)) comparator_11 (
    .a(counter_5_q), .b(out_11), .lt(comparator_11_lt));  // open: gt, eq
  Subtractor #(.width(5)) subtractor_2 (.a(out_8), .b(counter_4_q), .out(subtractor_2_out));  // open: bin, bout
  Subtractor #(.width(5)) subtractor_3 (.a(counter_4_q), .b(out_8), .out(subtractor_3_out));  // open: bin, bout
  assign controlled_buffer_1_out = not_3_out ? out_4 : 5'bz;  // Controlled_Buffer controlled_buffer_3
  not not_3 (not_3_out, and_4_out);
  or or_4 (or_4_out, comparator_7_eq, and_7_out);
  assign controlled_buffer_2_out = not_4_out ? out_7 : 5'bz;  // Controlled_Buffer controlled_buffer_4
  not not_4 (not_4_out, and_4_out);
  or or_5 (or_5_out, comparator_8_eq, comparator_9_eq);
  Comparator #(.mode("unsigned"), .width(5)) comparator_12 (
    .a(out_10), .b(out_8), .lt(comparator_12_lt));  // open: gt, eq
  Comparator #(.mode("unsigned"), .width(5)) comparator_13 (
    .a(out_8), .b(out_11), .lt(comparator_13_lt));  // open: gt, eq
  nor nor_1 (nor_1_out, comparator_10_lt, comparator_11_lt);
  not not_5 (not_5_out, nor_1_out);
  Comparator #(.mode("unsigned"), .width(5)) comparator_14 (
    .a(subtractor_2_out), .b(subtractor_3_out), .gt(comparator_14_gt));  // open: eq, lt
  J_K_Flip_Flop j_k_ff_1 (.J(or_4_out), .K(or_4_out), .clk(or_4_out), .Q(j_k_ff_1_q));  // open: Qn, preset, reset
  J_K_Flip_Flop j_k_ff_2 (.J(or_5_out), .K(or_5_out), .clk(or_5_out), .Q(j_k_ff_2_q));  // open: Qn, preset, reset
  nor nor_2 (nor_2_out, comparator_12_lt, comparator_13_lt);
  Multiplexer #(.width(5)) multiplexer_1 (
    .in0(subtractor_2_out), .in1(subtractor_3_out), .out(out_14), .sel(comparator_14_gt));
  not not_6 (not_6_out, nor_2_out);
  Button button_1 (.out(button_1_out));
  Button button_2 (.out(button_2_out));
  Multiplexer #(.width(5)) multiplexer_2 (
    .in0(controlled_buffer_1_out), .in1({5{1'b1}}), .out(multiplexer_2_out), .sel(not_2_out));
  Multiplexer #(.width(5)) multiplexer_3 (
    .in0(controlled_buffer_2_out), .in1(counter_5_q), .out(multiplexer_3_out), .sel(not_2_out));
  Multiplexer multiplexer_4 (.in0(not_4_out), .in1(not_5_out), .out(multiplexer_4_out[2]), .sel(not_2_out));
  and and_7 (and_7_out, comparator_6_eq, nor_2_out);
  and and_8 (and_8_out, comparator_6_eq, not_6_out);
  // RGB_Video #(.cursor("No Cursor"), .height(32), .scale(8), .width(32)) rgb_video_1: pin names not known; wires that end beside it: rgb_video_1_p1, 1'b1, multiplexer_2_out, multiplexer_3_out, {{2{multiplexer_4_out[2]}}, 1'b0}
  Clock clock_5 (.out(rgb_video_1_p1));
  Counter #(.max('hf), .width(4)) counter_6 (
    .clr(button_3_out), .count(1'b1), .clk(and_8_out), .Q(counter_6_q));  // open: load, up, D, carry
  Register #(.width(3)) register_3 (.D(out_14[2:0]), .en(1'b1), .clk(and_7_out), .Q(register_3_q));  // open: clr
  Counter #(.max('h7), .width(3)) counter_7 (
    .clr(or_6_out), .count(1'b1), .clk(and_4_out), .Q(counter_7_q));  // open: load, up, D, carry
  or or_6 (or_6_out, and_7_out, or_3_out);
  Hex_Digit_Display #(.decimalPoint("false")) hex_digit_display_1 (.value(counter_6_q));
  Button button_3 (.out(button_3_out));
  Subtractor #(.width(3)) subtractor_4 (.a(3'b100), .b(register_3_q), .out(subtractor_4_out));  // open: bin, bout
  Decoder #(.select(3)) decoder_1 (
    .out0(decoder_1_out0), .out1(decoder_1_out1), .out2(decoder_1_out2), .out3(decoder_1_out3),
    .out4(decoder_1_out4), .out5(decoder_1_out5), .out6(decoder_1_out6), .out7(decoder_1_out7),
    .sel(counter_7_q));  // open: en
  Multiplexer #(.select(3)) multiplexer_5 (
    .in0(decoder_1_out0), .in1(decoder_1_out1), .in2(decoder_1_out2), .in3(decoder_1_out3),
    .in4(decoder_1_out4), .in5(decoder_1_out5), .in6(decoder_1_out6), .in7(decoder_1_out7),
    .out(multiplexer_5_out), .sel(subtractor_4_out));

  assign out_6 = out_5;
  assign out_9 = out_8;
  assign out_12 = out_10;
  assign out_13 = out_11;

  // Notes on the sheet:
  //   X
  //   Y
endmodule

module decoder (
  input  [7:0] in_1
);

  wire not_1_out, not_2_out, not_3_out, not_4_out, not_5_out, not_6_out, not_7_out, not_8_out, undriven,
       undriven_2, undriven_3, undriven_4, undriven_5, undriven_6, undriven_7, undriven_8;

  not not_1 (not_1_out, in_1[0]);
  not not_2 (not_2_out, in_1[6]);
  not not_3 (not_3_out, in_1[5]);
  not not_4 (not_4_out, in_1[4]);
  not not_5 (not_5_out, in_1[3]);
  not not_6 (not_6_out, in_1[2]);
  not not_7 (not_7_out, in_1[1]);
  not not_8 (not_8_out, in_1[7]);
  // AND_Gate and_1 has open pins: in0=not_1_out, in1=not_2_out, in2=not_3_out, in3=not_4_out, in4=not_5_out, in5=not_6_out, in6=not_7_out, in7=not_8_out, out=open
  // AND_Gate and_2 has open pins: in0=in_1[0], in1=not_2_out, in2=not_3_out, in3=not_4_out, in4=not_5_out, in5=not_6_out, in6=not_7_out, in7=not_8_out, out=open
  // AND_Gate and_3 has open pins: in0=not_1_out, in1=in_1[6], in2=not_3_out, in3=not_4_out, in4=not_5_out, in5=not_6_out, in6=not_7_out, in7=not_8_out, out=open
  // AND_Gate and_4 has open pins: in0=in_1[0], in1=in_1[6], in2=not_3_out, in3=not_4_out, in4=not_5_out, in5=not_6_out, in6=not_7_out, in7=not_8_out, out=open
  // AND_Gate and_5 has open pins: in0=undriven, in1=undriven_2, in2=undriven_3, in3=undriven_4, in4=undriven_5, in5=undriven_6, in6=undriven_7, in7=undriven_8, out=open
endmodule

module Unsigned_adder (
  input  [4:0] in_1,
  input  [4:0] in_2,
  output [4:0] out_3
);

  wire [6:5] adder_1_out;

  Adder #(.width(7)) adder_1 (.a({2'b00, in_1}), .b({2'b00, in_2}), .out({adder_1_out, out_3}));  // open: cin, cout
endmodule
